// Logisim project 4-bit_ALU.circ as structural Verilog: 1 circuit, main circuit main
module main (
  input  [1:0] S1_S0,
  input  C,
  input  [3:0] A,
  input  [3:0] B,
  input  [1:0] S1_S0_2,
  input  in_6,
  input  [3:0] A_2,
  input  [3:0] B_2,
  output C_2,
  output [3:0] D
);

  wire adder_1_cout, adder_2_cout, adder_3_cout, and_1_out, and_2_out, and_3_out, and_4_out,
       multiplexer_1_out, multiplexer_2_out, multiplexer_3_out, multiplexer_4_out, not_1_out, not_2_out,
       not_3_out, not_4_out, not_5_out, not_6_out, not_7_out, not_8_out, not_9_out, or_1_out, or_2_out,
       or_3_out, or_4_out, xor_1_out, xor_2_out, xor_3_out, xor_4_out;
  wire [3:0] adder_1_out, multiplexer_8_out;

  not not_1 (not_1_out, B[0]);
  not not_2 (not_2_out, B[1]);
  not not_3 (not_3_out, B[2]);
  not not_4 (not_4_out, B[3]);
  not not_5 (not_5_out, 1'b1);
  or or_1 (or_1_out, A_2[3], B_2[3]);
  and and_1 (and_1_out, A_2[3], B_2[3]);
  xor xor_1 (xor_1_out, A_2[3], B_2[3]);
  not not_6 (not_6_out, A_2[3]);
  or or_2 (or_2_out, A_2[2], B_2[2]);
  and and_2 (and_2_out, A_2[2], B_2[2]);
  xor xor_2 (xor_2_out, A_2[2], B_2[2]);
  not not_7 (not_7_out, A_2[2]);
  or or_3 (or_3_out, A_2[1], B_2[1]);
  and and_3 (and_3_out, A_2[1], B_2[1]);
  xor xor_3 (xor_3_out, A_2[1], B_2[1]);
  not not_8 (not_8_out, A_2[1]);
  or or_4 (or_4_out, A_2[0], B_2[0]);
  and and_4 (and_4_out, A_2[0], B_2[0]);
  xor xor_4 (xor_4_out, A_2[0], B_2[0]);
  not not_9 (not_9_out, A_2[0]);
  Multiplexer #(.select(2)) multiplexer_1 (
    .in0(B[0]), .in1(not_1_out), .in2(not_5_out), .in3(1'b1), .out(multiplexer_1_out), .sel(S1_S0));  // open: en
  Multiplexer #(.select(2)) multiplexer_2 (
    .in0(B[1]), .in1(not_2_out), .in2(not_5_out), .in3(1'b1), .out(multiplexer_2_out), .sel(S1_S0));  // open: en
  Multiplexer #(.select(2)) multiplexer_3 (
    .in0(B[2]), .in1(not_3_out), .in2(not_5_out), .in3(1'b1), .out(multiplexer_3_out), .sel(S1_S0));  // open: en
  Multiplexer #(.select(2)) multiplexer_4 (
    .in0(B[3]), .in1(not_4_out), .in2(not_5_out), .in3(1'b1), .out(multiplexer_4_out), .sel(S1_S0));  // open: en
  Adder #(.width(1)) adder_1 (.a(A[0]), .b(multiplexer_1_out), .out(adder_1_out[0]), .cin(C), .cout(adder_1_cout));
  Adder #(.width(1)) adder_2 (
    .a(A[1]), .b(multiplexer_2_out), .out(adder_1_out[1]), .cin(adder_1_cout), .cout(adder_2_cout));
  Adder #(.width(1)) adder_3 (
    .a(A[2]), .b(multiplexer_3_out), .out(adder_1_out[2]), .cin(adder_2_cout), .cout(adder_3_cout));
  Adder #(.width(1)) adder_4 (.a(A[3]), .b(multiplexer_4_out), .out(adder_1_out[3]), .cin(adder_3_cout), .cout(C_2));
  Multiplexer #(.select(2)) multiplexer_5 (
    .in0(or_1_out), .in1(and_1_out), .in2(xor_1_out), .in3(not_6_out), .out(multiplexer_8_out[3]),
    .sel(S1_S0_2));  // open: en
  Multiplexer #(.select(2)) multiplexer_6 (
    .in0(or_2_out), .in1(and_2_out), .in2(xor_2_out), .in3(not_7_out), .out(multiplexer_8_out[2]),
    .sel(S1_S0_2));  // open: en
  Multiplexer #(.select(2)) multiplexer_7 (
    .in0(or_3_out), .in1(and_3_out), .in2(xor_3_out), .in3(not_8_out), .out(multiplexer_8_out[1]),
    .sel(S1_S0_2));  // open: en
  Multiplexer #(.select(2)) multiplexer_8 (
    .in0(or_4_out), .in1(and_4_out), .in2(xor_4_out), .in3(not_9_out), .out(multiplexer_8_out[0]),
    .sel(S1_S0_2));  // open: en
  Multiplexer #(.width(4)) multiplexer_9 (.in0(adder_1_out), .in1(multiplexer_8_out), .out(D), .sel(in_6));  // open: en

  // Notes on the sheet:
  //   B0
  //   B1
  //   B2
  //   B3
  //   4 - Bit Logical Unit
  //   A3 and B3
  //   A2 and B2
  //   A1 and B1
  //   A0 and B0
  //   4-Bit Arithmetic Circuit
  //   A3
  //   A0
  //   A1
  //   A2
  //   Logical Output
  //   Arithmetic Output
endmodule
